// Logisim project Circuit.circ as structural Verilog
// reg
module shiftRightReg (
  input  i_0,
  input  i_1,
  input  i_2,
  input  i_3,
  input  i_4,
  input  i_5,
  input  i_6,
  input  i_7,
  input  Clock,
  input  Enable,
  input  Load,
  output out_12
);

  wire d_ff_1_q, d_ff_3_q, d_ff_4_q, d_ff_5_q, d_ff_6_q, d_ff_7_q, d_ff_8_q, multiplexer_1_out,
       multiplexer_2_out, multiplexer_3_out, multiplexer_4_out, multiplexer_5_out, multiplexer_6_out,
       multiplexer_7_out, multiplexer_8_out, multiplexer_9_out, multiplexer_10_out, multiplexer_11_out,
       multiplexer_12_out, multiplexer_13_out, multiplexer_14_out, multiplexer_15_out, multiplexer_16_out,
       undriven, undriven_2, undriven_3, undriven_4, undriven_5, undriven_6, undriven_7, undriven_8;

  Multiplexer multiplexer_1 (.in0(1'b0), .in1(i_0), .out(multiplexer_1_out), .sel(Load));
  D_Flip_Flop d_ff_1 (.D(multiplexer_2_out), .clk(Clock), .Q(d_ff_1_q), .reset(undriven));  // open: Qn, preset
  Multiplexer multiplexer_2 (.in0(d_ff_1_q), .in1(multiplexer_1_out), .out(multiplexer_2_out), .sel(Enable));
  D_Flip_Flop d_ff_2 ();  // open: D, clk, Q, Qn, preset, reset
  Multiplexer multiplexer_3 (.in0(d_ff_1_q), .in1(i_1), .out(multiplexer_3_out), .sel(Load));
  D_Flip_Flop d_ff_3 (.D(multiplexer_4_out), .clk(Clock), .Q(d_ff_3_q), .reset(undriven_2));  // open: Qn, preset
  Multiplexer multiplexer_4 (.in0(d_ff_3_q), .in1(multiplexer_3_out), .out(multiplexer_4_out), .sel(Enable));
  Multiplexer multiplexer_5 (.in0(d_ff_4_q), .in1(multiplexer_6_out), .out(multiplexer_5_out), .sel(Enable));
  Multiplexer multiplexer_6 (.in0(d_ff_3_q), .in1(i_2), .out(multiplexer_6_out), .sel(Load));
  D_Flip_Flop d_ff_4 (.D(multiplexer_5_out), .clk(Clock), .Q(d_ff_4_q), .reset(undriven_3));  // open: Qn, preset
  Multiplexer multiplexer_7 (.in0(d_ff_4_q), .in1(i_3), .out(multiplexer_7_out), .sel(Load));
  D_Flip_Flop d_ff_5 (.D(multiplexer_8_out), .clk(Clock), .Q(d_ff_5_q), .reset(undriven_4));  // open: Qn, preset
  Multiplexer multiplexer_8 (.in0(d_ff_5_q), .in1(multiplexer_7_out), .out(multiplexer_8_out), .sel(Enable));
  Multiplexer multiplexer_9 (.in0(d_ff_5_q), .in1(i_4), .out(multiplexer_9_out), .sel(Load));
  Multiplexer multiplexer_10 (.in0(d_ff_6_q), .in1(multiplexer_9_out), .out(multiplexer_10_out), .sel(Enable));
  D_Flip_Flop d_ff_6 (.D(multiplexer_10_out), .clk(Clock), .Q(d_ff_6_q), .reset(undriven_5));  // open: Qn, preset
  Multiplexer multiplexer_11 (.in0(d_ff_6_q), .in1(i_5), .out(multiplexer_11_out), .sel(Load));
  Multiplexer multiplexer_12 (.in0(d_ff_7_q), .in1(multiplexer_11_out), .out(multiplexer_12_out), .sel(Enable));
  D_Flip_Flop d_ff_7 (.D(multiplexer_12_out), .clk(Clock), .Q(d_ff_7_q), .reset(undriven_6));  // open: Qn, preset
  Multiplexer multiplexer_13 (.in0(d_ff_7_q), .in1(i_6), .out(multiplexer_13_out), .sel(Load));
  Multiplexer multiplexer_14 (.in0(d_ff_8_q), .in1(multiplexer_13_out), .out(multiplexer_14_out), .sel(Enable));
  D_Flip_Flop d_ff_8 (.D(multiplexer_14_out), .clk(Clock), .Q(d_ff_8_q), .reset(undriven_7));  // open: Qn, preset
  Multiplexer multiplexer_15 (.in0(d_ff_8_q), .in1(i_7), .out(multiplexer_15_out), .sel(Load));
  Multiplexer multiplexer_16 (.in0(out_12), .in1(multiplexer_15_out), .out(multiplexer_16_out), .sel(Enable));
  D_Flip_Flop d_ff_9 (.D(multiplexer_16_out), .clk(Clock), .Q(out_12), .reset(undriven_8));  // open: Qn, preset
endmodule

module shiftLeftReg (
  input  i_0,
  input  i_1,
  input  i_2,
  input  i_3,
  input  i_4,
  input  i_5,
  input  i_6,
  input  i_7,
  input  Clock,
  input  Enable,
  input  Load,
  output out_12
);

  wire d_ff_2_q, d_ff_3_q, d_ff_4_q, d_ff_5_q, d_ff_6_q, d_ff_7_q, d_ff_8_q, multiplexer_1_out,
       multiplexer_2_out, multiplexer_3_out, multiplexer_4_out, multiplexer_5_out, multiplexer_6_out,
       multiplexer_7_out, multiplexer_8_out, multiplexer_9_out, multiplexer_10_out, multiplexer_11_out,
       multiplexer_12_out, multiplexer_13_out, multiplexer_14_out, multiplexer_15_out, multiplexer_16_out,
       undriven, undriven_2, undriven_3, undriven_4, undriven_5, undriven_6, undriven_7, undriven_8;

  Multiplexer multiplexer_1 (.in0(d_ff_2_q), .in1(i_0), .out(multiplexer_1_out), .sel(Load));
  D_Flip_Flop d_ff_1 (.D(multiplexer_2_out), .clk(Clock), .Q(out_12), .reset(undriven));  // open: Qn, preset
  Multiplexer multiplexer_2 (.in0(out_12), .in1(multiplexer_1_out), .out(multiplexer_2_out), .sel(Enable));
  LED led_1 (.in(out_12));
  Multiplexer multiplexer_3 (.in0(d_ff_3_q), .in1(i_1), .out(multiplexer_3_out), .sel(Load));
  D_Flip_Flop d_ff_2 (.D(multiplexer_4_out), .clk(Clock), .Q(d_ff_2_q), .reset(undriven_2));  // open: Qn, preset
  Multiplexer multiplexer_4 (.in0(d_ff_2_q), .in1(multiplexer_3_out), .out(multiplexer_4_out), .sel(Enable));
  Multiplexer multiplexer_5 (.in0(d_ff_3_q), .in1(multiplexer_6_out), .out(multiplexer_5_out), .sel(Enable));
  Multiplexer multiplexer_6 (.in0(d_ff_4_q), .in1(i_2), .out(multiplexer_6_out), .sel(Load));
  D_Flip_Flop d_ff_3 (.D(multiplexer_5_out), .clk(Clock), .Q(d_ff_3_q), .reset(undriven_3));  // open: Qn, preset
  Multiplexer multiplexer_7 (.in0(d_ff_5_q), .in1(i_3), .out(multiplexer_7_out), .sel(Load));
  D_Flip_Flop d_ff_4 (.D(multiplexer_8_out), .clk(Clock), .Q(d_ff_4_q), .reset(undriven_4));  // open: Qn, preset
  Multiplexer multiplexer_8 (.in0(d_ff_4_q), .in1(multiplexer_7_out), .out(multiplexer_8_out), .sel(Enable));
  Multiplexer multiplexer_9 (.in0(d_ff_6_q), .in1(i_4), .out(multiplexer_9_out), .sel(Load));
  Multiplexer multiplexer_10 (.in0(d_ff_5_q), .in1(multiplexer_9_out), .out(multiplexer_10_out), .sel(Enable));
  D_Flip_Flop d_ff_5 (.D(multiplexer_10_out), .clk(Clock), .Q(d_ff_5_q), .reset(undriven_5));  // open: Qn, preset
  Multiplexer multiplexer_11 (.in0(d_ff_7_q), .in1(i_5), .out(multiplexer_11_out), .sel(Load));
  Multiplexer multiplexer_12 (.in0(d_ff_6_q), .in1(multiplexer_11_out), .out(multiplexer_12_out), .sel(Enable));
  D_Flip_Flop d_ff_6 (.D(multiplexer_12_out), .clk(Clock), .Q(d_ff_6_q), .reset(undriven_6));  // open: Qn, preset
  Multiplexer multiplexer_13 (.in0(d_ff_8_q), .in1(i_6), .out(multiplexer_13_out), .sel(Load));
  Multiplexer multiplexer_14 (.in0(d_ff_7_q), .in1(multiplexer_13_out), .out(multiplexer_14_out), .sel(Enable));
  D_Flip_Flop d_ff_7 (.D(multiplexer_14_out), .clk(Clock), .Q(d_ff_7_q), .reset(undriven_7));  // open: Qn, preset
  Multiplexer multiplexer_15 (.in0(1'b0), .in1(i_7), .out(multiplexer_15_out), .sel(Load));
  Multiplexer multiplexer_16 (.in0(d_ff_8_q), .in1(multiplexer_15_out), .out(multiplexer_16_out), .sel(Enable));
  D_Flip_Flop d_ff_8 (.D(multiplexer_16_out), .clk(Clock), .Q(d_ff_8_q), .reset(undriven_8));  // open: Qn, preset
endmodule
